# Fritzing sketch setup (saved by Fritzing 0.9.9b)
breadboards: 1

parts:
  LED1 = LED - 5mm [color="Red (633nm)" current=0.030 package="5 mm [THT]"]
  R1 = Resistor [tolerance=±5% power=0.25 resistance=220 package=THT]
  R2 = PHOTOCELL [package=photocell-kit]
  J1 = STM32 Nucleo boards
  R3 = Resistor [tolerance=±5% power=0.25 resistance=470 package=THT]

nets:
  N1: LED1.cathode, J1.GND, R3.Pin_1
  N2: LED1.anode, R1.Pin_0
  N3: R1.Pin_1, J1.A5/SCL
  N4: R2.P$1, J1.3V3
  N5: R2.P$2, J1.D3_PWM, R3.Pin_0
